// Logisim project Full.circ as structural Verilog: 1 circuit, main circuit main
module main (
  input  Add_Sub,
  input  Multiplication_mode,
  input  A2,
  input  A1,
  input  A0,
  input  B2,
  input  B1,
  input  B0
);

  wire main_1_r0, main_1_r1, main_1_r2, main_1_r3, main_1_s, main_2_rl0, main_2_rl1, main_2_rl2, main_2_rl3,
       main_2_rr0, main_2_rr1, main_2_rr2, main_2_rr3, main_2_s, multiplexer_1_out, multiplexer_2_out,
       n7_segment_display_driver_1_p1, n7_segment_display_driver_1_p3, n7_segment_display_driver_1_p4,
       n7_segment_display_driver_1_p5, n7_segment_display_driver_1_p6, n7_segment_display_driver_1_p7,
       n7_segment_display_driver_1_p8, n7_segment_display_driver_1_p9, n7_segment_display_driver_1_p10,
       n7_segment_display_driver_1_p11, n7_segment_display_driver_2_p1, n7_segment_display_driver_2_p2,
       n7_segment_display_driver_2_p3, n7_segment_display_driver_2_p4, n7_segment_display_driver_2_p5,
       n7_segment_display_driver_2_p6, n7_segment_display_driver_2_p7, n7_segment_display_driver_2_p8,
       n7_segment_display_driver_2_p9, n7_segment_display_driver_2_p10, n7_segment_display_driver_2_p11;

  Add_Lib_main main_1 (
    .A2(A2), .A1(A1), .A0(A0), .B2(B2), .B1(B1), .B0(B0), .CTRL(Add_Sub), .S(main_1_s), .R3(main_1_r3),
    .R2(main_1_r2), .R1(main_1_r1), .R0(main_1_r0));
  Multi_Lib_main main_2 (
    .A2(A2), .A1(A1), .A0(A0), .B2(B2), .B1(B1), .B0(B0), .S(main_2_s), .RL3(main_2_rl3), .RL2(main_2_rl2),
    .RL1(main_2_rl1), .RL0(main_2_rl0), .RR3(main_2_rr3), .RR2(main_2_rr2), .RR1(main_2_rr1), .RR0(main_2_rr0));
  Multiplexer #(.enable("false")) multiplexer_1 (
    .in0(main_1_s), .in1(main_2_s), .out(multiplexer_1_out), .sel(Multiplication_mode));
  Multiplexer #(.enable("false")) multiplexer_2 (
    .in0(1'b0), .in1(main_2_rl3), .out(multiplexer_2_out), .sel(Multiplication_mode));
  _7_Segment_Display u_7_segment_display_1 (.g(multiplexer_1_out));  // open: f, a, b, e, d, c, dp
  // _7_segment_display_driver 7_segment_display_driver_1: pin names not known; wires that end beside it: n7_segment_display_driver_1_p1, multiplexer_2_out, n7_segment_display_driver_1_p3, n7_segment_display_driver_1_p4, n7_segment_display_driver_1_p5, n7_segment_display_driver_1_p6, n7_segment_display_driver_1_p7, n7_segment_display_driver_1_p8, n7_segment_display_driver_1_p9, n7_segment_display_driver_1_p10, n7_segment_display_driver_1_p11
  Multiplexer #(.enable("false")) multiplexer_3 (
    .in0(1'b0), .in1(main_2_rl2), .out(n7_segment_display_driver_1_p4), .sel(Multiplication_mode));
  Multiplexer #(.enable("false")) multiplexer_4 (
    .in0(1'b0), .in1(main_2_rl1), .out(n7_segment_display_driver_1_p6), .sel(Multiplication_mode));
  _7_Segment_Display u_7_segment_display_2 (
    .g(n7_segment_display_driver_1_p11), .f(n7_segment_display_driver_1_p10),
    .a(n7_segment_display_driver_1_p1), .b(n7_segment_display_driver_1_p3),
    .e(n7_segment_display_driver_1_p9), .d(n7_segment_display_driver_1_p7), .c(n7_segment_display_driver_1_p5));  // open: dp
  Multiplexer #(.enable("false")) multiplexer_5 (
    .in0(1'b0), .in1(main_2_rl0), .out(n7_segment_display_driver_1_p8), .sel(Multiplication_mode));
  _7_Segment_Display u_7_segment_display_3 (
    .g(n7_segment_display_driver_2_p11), .f(n7_segment_display_driver_2_p10),
    .a(n7_segment_display_driver_2_p1), .b(n7_segment_display_driver_2_p3),
    .e(n7_segment_display_driver_2_p9), .d(n7_segment_display_driver_2_p7), .c(n7_segment_display_driver_2_p5));  // open: dp
  // _7_segment_display_driver 7_segment_display_driver_2: pin names not known; wires that end beside it: n7_segment_display_driver_2_p1, n7_segment_display_driver_2_p2, n7_segment_display_driver_2_p3, n7_segment_display_driver_2_p4, n7_segment_display_driver_2_p5, n7_segment_display_driver_2_p6, n7_segment_display_driver_2_p7, n7_segment_display_driver_2_p8, n7_segment_display_driver_2_p9, n7_segment_display_driver_2_p10, n7_segment_display_driver_2_p11
  Multiplexer #(.enable("false")) multiplexer_6 (
    .in0(main_1_r3), .in1(main_2_rr3), .out(n7_segment_display_driver_2_p2), .sel(Multiplication_mode));
  Multiplexer #(.enable("false")) multiplexer_7 (
    .in0(main_1_r2), .in1(main_2_rr2), .out(n7_segment_display_driver_2_p4), .sel(Multiplication_mode));
  Multiplexer #(.enable("false")) multiplexer_8 (
    .in0(main_1_r1), .in1(main_2_rr1), .out(n7_segment_display_driver_2_p6), .sel(Multiplication_mode));
  Multiplexer #(.enable("false")) multiplexer_9 (
    .in0(main_1_r0), .in1(main_2_rr0), .out(n7_segment_display_driver_2_p8), .sel(Multiplication_mode));
endmodule
