// Logisim project Multiplication.circ as structural Verilog: 1 circuit, main circuit main
module main (
  input  A2,
  input  A1,
  input  A0,
  input  B2,
  input  B1,
  input  B0,
  output R0,
  output R1,
  output R2,
  output R3,
  output R4,
  output R5
);

  wire B0A1_out, B0A2_out, B1A0_out, B1A1_out, B1A2_out, B2A0_out, B2A1_out, B2A2_out,
       full_adder_1_carry_out, full_adder_1_output, full_adder_2_carry_out, full_adder_2_output,
       full_adder_3_carry_out, full_adder_4_carry_out, half_adder_1_carry_out, half_adder_2_carry_out;

  and B0A0 (R0, B0, A0);
  and B0A1 (B0A1_out, B0, A1);
  nand B0A2 (B0A2_out, B0, A2);
  and B1A0 (B1A0_out, B1, A0);
  and B1A1 (B1A1_out, B1, A1);
  nand B1A2 (B1A2_out, B1, A2);
  Half___Adder half_adder_1 (.Inp1(B1A0_out), .Inp2(B0A1_out), .Result(R1), .Carry_out(half_adder_1_carry_out));
  Full___Adder full_adder_1 (
    .Carry_in(half_adder_1_carry_out), .Inp1(B1A1_out), .Inp2(B0A2_out), .Output(full_adder_1_output),
    .Carry_out(full_adder_1_carry_out));
  Full___Adder full_adder_2 (
    .Carry_in(full_adder_1_carry_out), .Inp1(B1A2_out), .Inp2(1'b1), .Output(full_adder_2_output),
    .Carry_out(full_adder_2_carry_out));
  nand B2A0 (B2A0_out, B2, A0);
  nand B2A1 (B2A1_out, B2, A1);
  and B2A2 (B2A2_out, B2, A2);
  Half___Adder half_adder_2 (
    .Inp1(full_adder_1_output), .Inp2(B2A0_out), .Result(R2), .Carry_out(half_adder_2_carry_out));
  Full___Adder full_adder_3 (
    .Carry_in(half_adder_2_carry_out), .Inp1(B2A1_out), .Inp2(full_adder_2_output), .Output(R3),
    .Carry_out(full_adder_3_carry_out));
  Full___Adder full_adder_4 (
    .Carry_in(full_adder_3_carry_out), .Inp1(B2A2_out), .Inp2(full_adder_2_carry_out), .Output(R4),
    .Carry_out(full_adder_4_carry_out));
  Half___Adder half_adder_3 (.Inp1(full_adder_4_carry_out), .Inp2(1'b1), .Result(R5));  // open: Carry_out
endmodule
